// Logisim project 3_player_rock_paper_scissor.circ as structural Verilog: 1 circuit, main circuit main
module main (
);

  wire and_4_out, and_5_out, and_6_out, and_7_out, and_8_out, and_9_out, and_10_out, and_11_out, and_12_out,
       and_13_out, and_14_out, and_15_out, and_16_out, and_17_out, and_18_out, and_19_out, and_20_out,
       and_21_out, and_22_out, and_23_out, and_24_out, and_25_out, and_26_out, and_27_out, and_28_out,
       and_29_out, and_30_out, dipswitch_1_p1, dipswitch_1_p2, dipswitch_1_p3, dipswitch_1_p4,
       dipswitch_1_p5, dipswitch_2_p3, dipswitch_2_p4, dipswitch_2_p5, dipswitch_2_p6, dipswitch_3_p3,
       dipswitch_3_p5, dipswitch_3_p9, dipswitch_3_p10, not_3_out, not_4_out, or_1_out, or_2_out, or_3_out,
       or_4_out, or_5_out, or_6_out, or_7_out, or_8_out, or_9_out, or_10_out, or_11_out, or_12_out;

  // DipSwitch #(.number(2)) dipswitch_1: pin names not known; wires that end beside it: dipswitch_1_p1, dipswitch_1_p2, dipswitch_1_p3, dipswitch_1_p4, dipswitch_1_p5
  // DipSwitch #(.number(2)) dipswitch_2: pin names not known; wires that end beside it: dipswitch_1_p1, dipswitch_1_p2, dipswitch_2_p3, dipswitch_2_p4, dipswitch_2_p5, dipswitch_2_p6
  not not_1 (dipswitch_2_p5, dipswitch_1_p1);
  not not_2 (dipswitch_2_p6, dipswitch_1_p2);
  not not_3 (not_3_out, dipswitch_2_p3);
  not not_4 (not_4_out, dipswitch_2_p4);
  // DipSwitch #(.number(2)) dipswitch_3: pin names not known; wires that end beside it: dipswitch_2_p3, dipswitch_2_p4, dipswitch_3_p3, dipswitch_3_p3, dipswitch_3_p5, dipswitch_3_p5, not_3_out, not_4_out, dipswitch_3_p9, dipswitch_3_p10
  not not_5 (dipswitch_3_p9, dipswitch_3_p3);
  not not_6 (dipswitch_3_p10, dipswitch_3_p5);
  and and_1 (dipswitch_1_p5, dipswitch_3_p3, dipswitch_3_p5);
  and and_2 (dipswitch_1_p4, dipswitch_3_p3, dipswitch_3_p10);
  and and_3 (dipswitch_1_p3, dipswitch_3_p9, dipswitch_3_p5);
  and and_4 (and_4_out, dipswitch_2_p3, dipswitch_2_p4);
  and and_5 (and_5_out, dipswitch_2_p3, not_4_out);
  and and_6 (and_6_out, not_3_out, dipswitch_2_p4);
  and and_7 (and_7_out, dipswitch_1_p1, dipswitch_1_p2);
  and and_8 (and_8_out, dipswitch_1_p1, dipswitch_2_p6);
  and and_9 (and_9_out, dipswitch_2_p5, dipswitch_1_p2);
  and and_10 (and_10_out, and_7_out, and_5_out, dipswitch_1_p4);
  and and_11 (and_11_out, and_8_out, and_6_out, dipswitch_1_p3);
  and and_12 (and_12_out, and_9_out, and_4_out, dipswitch_1_p5);
  and and_13 (and_13_out, dipswitch_1_p5, and_5_out, and_8_out);
  and and_14 (and_14_out, dipswitch_1_p4, and_6_out, and_9_out);
  and and_15 (and_15_out, dipswitch_1_p3, and_4_out, and_7_out);
  and and_16 (and_16_out, and_4_out, and_8_out, dipswitch_1_p4);
  and and_17 (and_17_out, and_5_out, and_9_out, dipswitch_1_p3);
  and and_18 (and_18_out, and_6_out, and_7_out, dipswitch_1_p5);
  and and_19 (and_19_out, and_7_out, and_4_out, dipswitch_1_p5);
  and and_20 (and_20_out, and_8_out, and_5_out, dipswitch_1_p4);
  and and_21 (and_21_out, and_9_out, and_6_out, dipswitch_1_p3);
  and and_22 (and_22_out, and_7_out, and_4_out, dipswitch_1_p4);
  and and_23 (and_23_out, and_8_out, and_5_out, dipswitch_1_p3);
  and and_24 (and_24_out, and_9_out, and_6_out, dipswitch_1_p5);
  and and_25 (and_25_out, and_7_out, dipswitch_1_p5, and_5_out);
  and and_26 (and_26_out, and_8_out, dipswitch_1_p4, and_6_out);
  and and_27 (and_27_out, and_9_out, dipswitch_1_p3, and_4_out);
  and and_28 (and_28_out, dipswitch_1_p3, and_6_out, and_7_out);
  and and_29 (and_29_out, dipswitch_1_p4, and_5_out, and_9_out);
  and and_30 (and_30_out, dipswitch_1_p5, and_4_out, and_8_out);
  or or_1 (or_1_out, and_10_out, and_11_out, and_12_out);
  or or_2 (or_2_out, and_13_out, and_14_out, and_15_out);
  or or_3 (or_3_out, and_16_out, and_17_out, and_18_out);
  or or_4 (or_4_out, and_19_out, and_20_out, and_21_out);
  or or_5 (or_5_out, and_22_out, and_23_out, and_24_out);
  or or_6 (or_6_out, and_25_out, and_26_out, and_27_out);
  or or_7 (or_7_out, and_28_out, and_29_out, and_30_out);
  or or_8 (or_8_out, or_4_out, or_5_out, or_6_out, or_7_out);
  or or_9 (or_9_out, or_1_out, or_3_out);
  or or_10 (or_10_out, or_1_out, or_2_out, or_3_out, or_8_out);
  or or_11 (or_11_out, or_2_out, or_8_out, or_3_out);
  _7_Segment_Display u_7_segment_display_1 (
    .g(or_9_out), .f(or_10_out), .a(or_10_out), .b(or_12_out), .e(or_10_out), .d(or_11_out), .c(or_12_out));  // open: dp
  or or_12 (or_12_out, or_9_out, or_8_out);

  // Notes on the sheet:
  //   Player A
  //   Player B
  //   Player C
  //   ROCK 11
  //   SCISSOR 10
  //   PAPER 01
  //   R
  //   S
  //   P
  //   R
  //   S
  //   P
  //   R
  //   S
  //   P
  //   B C tie
  //   A wins
  //   C wins
  //   B wins
  //   A B C tie
  //   A B tie
  //   A C tie
endmodule
